// Logisim project Full Adder.circ as structural Verilog: 1 circuit, main circuit main
module main (
  input  X,
  input  Y,
  input  Z___Carry_In,
  output S___Sum,
  output C___Carry_Out
);

  wire and_1_out, and_2_out, xor_1_out;

  xor xor_1 (xor_1_out, X, Y);
  xor xor_2 (S___Sum, xor_1_out, Z___Carry_In);
  and and_1 (and_1_out, Z___Carry_In, xor_1_out);
  and and_2 (and_2_out, Y, X);
  or or_1 (C___Carry_Out, and_1_out, and_2_out);
endmodule
