// Logisim project HW4Q3.circ as structural Verilog: 1 circuit, main circuit main
module main (
  input  X___1_s,
  input  Y___2_s,
  input  Z___4_s,
  output A___1_s,
  output B___2_s,
  output C___4_s
);

  wire and_1_out, and_2_out, and_3_out, and_4_out, and_5_out, and_6_out, not_1_out, not_2_out, not_3_out,
       not_4_out;

  not not_1 (not_1_out, X___1_s);
  not not_2 (not_2_out, Y___2_s);
  not not_3 (not_3_out, Z___4_s);
  and and_1 (and_1_out, X___1_s, not_3_out);
  and and_2 (and_2_out, not_1_out, Z___4_s);
  and and_3 (and_3_out, Z___4_s, not_1_out, not_2_out);
  and and_4 (and_4_out, X___1_s, Y___2_s, Z___4_s);
  and and_5 (and_5_out, not_2_out, not_3_out);
  not not_4 (not_4_out, Y___2_s);
  or or_1 (A___1_s, and_1_out, and_2_out);
  and and_6 (and_6_out, X___1_s, Z___4_s, not_4_out);
  or or_2 (B___2_s, and_3_out, and_4_out, and_5_out);
  or or_3 (C___4_s, and_6_out, Y___2_s);
endmodule
