// Logisim project HW5 Q4.circ as structural Verilog: 1 circuit, main circuit main
module main (
  output out_1,
  output out_2,
  output out_3
);

  wire and_1_out, and_2_out, clock_1_out, not_1_out, not_2_out, not_3_out, not_4_out, not_5_out, or_1_out,
       or_2_out, or_3_out, or_4_out;

  not not_1 (not_1_out, out_1);
  not not_2 (not_2_out, out_2);
  not not_3 (not_3_out, out_3);
  or or_1 (or_1_out, not_3_out, out_2);
  or or_2 (or_2_out, out_3, out_2);
  not not_4 (not_4_out, out_3);
  or or_3 (or_3_out, not_4_out, not_5_out);
  not not_5 (not_5_out, out_1);
  and and_1 (and_1_out, not_1_out, not_2_out);
  and and_2 (and_2_out, out_1, out_2);
  or or_4 (or_4_out, and_1_out, and_2_out);
  Clock clock_1 (.out(clock_1_out));
  J_K_Flip_Flop j_k_ff_1 (.J(or_1_out), .clk(clock_1_out), .K(or_2_out), .Q(out_1));  // open: Qn, preset, en, reset
  J_K_Flip_Flop j_k_ff_2 (.J(or_3_out), .clk(clock_1_out), .K(or_3_out), .Q(out_2));  // open: Qn, preset, en, reset
  J_K_Flip_Flop j_k_ff_3 (.J(or_4_out), .clk(clock_1_out), .K(out_1), .Q(out_3));  // open: Qn, preset, en, reset

  // Notes on the sheet:
  //   ~C + B
  //   C + B
  //   ~C + ~A  2x
  //   ~A~B
  //   AB
  //   State  7 -> 2 -> 4 -> 6 -> 1 -> 3 -> 5 -> 0 -> repeat at 7
  //   A
  //   B
  //   C
  //   A              B              C
endmodule
