// Logisim project Q1verify.circ as structural Verilog: 1 circuit, main circuit main
module main (
  input  A,
  input  B,
  input  C,
  input  D,
  output out_5
);

  wire nand_1_out, nor_1_out, not_1_out, or_1_out, xnor_1_out;

  xnor xnor_1 (xnor_1_out, A, C);
  not not_1 (not_1_out, B);
  or or_1 (or_1_out, B, D);
  nor nor_1 (nor_1_out, xnor_1_out, not_1_out);
  nand nand_1 (nand_1_out, not_1_out, or_1_out);
  and and_1 (out_5, nor_1_out, nand_1_out);

  // Notes on the sheet:
  //   XNOR
  //   OR
  //   NOR
  //   NAND
endmodule
